// Logisim project Circuito .circ as structural Verilog: 1 circuit, main circuit main
module main (
  input  A,
  input  B,
  input  C,
  input  D,
  output W,
  output X,
  output Y,
  output Z
);

  wire and_1_out, and_2_out, and_3_out, and_4_out, and_5_out, and_6_out, and_7_out, and_8_out, and_9_out,
       and_10_out, and_11_out, and_12_out, and_14_out, and_15_out, and_16_out, and_17_out, and_18_out,
       and_19_out, and_20_out, and_21_out, and_22_out, and_23_out, not_1_out, not_2_out, not_3_out,
       not_4_out, not_5_out, not_6_out, not_7_out, not_8_out, not_9_out, not_10_out, not_11_out, not_12_out,
       not_13_out, not_14_out, not_15_out, not_16_out, not_17_out, not_18_out, not_19_out, not_20_out,
       not_21_out, or_1_out, or_2_out, or_3_out, xor_1_out;

  not not_1 (not_1_out, A);
  not not_2 (not_2_out, B);
  and and_1 (and_1_out, not_1_out, not_2_out);
  xor xor_1 (xor_1_out, D, C);
  not not_3 (not_3_out, A);
  not not_4 (not_4_out, A);
  not not_5 (not_5_out, C);
  not not_6 (not_6_out, B);
  not not_7 (not_7_out, D);
  and and_2 (and_2_out, D, B);
  not not_8 (not_8_out, A);
  not not_9 (not_9_out, D);
  not not_10 (not_10_out, B);
  not not_11 (not_11_out, C);
  not not_12 (not_12_out, A);
  not not_13 (not_13_out, D);
  not not_14 (not_14_out, B);
  not not_15 (not_15_out, C);
  not not_16 (not_16_out, D);
  not not_17 (not_17_out, B);
  and and_3 (and_3_out, not_17_out, not_18_out);
  not not_18 (not_18_out, C);
  not not_19 (not_19_out, D);
  and and_4 (and_4_out, not_3_out, B);
  and and_5 (and_5_out, A, not_20_out);
  not not_20 (not_20_out, B);
  not not_21 (not_21_out, C);
  and and_6 (and_6_out, not_4_out, not_5_out);
  and and_7 (and_7_out, not_6_out, not_7_out);
  and and_8 (and_8_out, not_8_out, B);
  and and_9 (and_9_out, C, not_9_out);
  and and_10 (and_10_out, A, not_10_out);
  and and_11 (and_11_out, not_11_out, D);
  and and_12 (and_12_out, not_12_out, not_13_out);
  and and_13 (W, and_1_out, xor_1_out);
  or or_1 (or_1_out, and_7_out, and_2_out);
  and and_14 (and_14_out, and_8_out, and_9_out);
  and and_15 (and_15_out, and_10_out, and_11_out);
  and and_16 (and_16_out, A, not_14_out);
  and and_17 (and_17_out, not_15_out, not_16_out);
  and and_18 (and_18_out, and_3_out, not_19_out);
  and and_19 (and_19_out, and_4_out, C);
  and and_20 (and_20_out, and_5_out, not_21_out);
  and and_21 (and_21_out, and_6_out, or_1_out);
  and and_22 (and_22_out, and_16_out, and_17_out);
  or or_2 (or_2_out, and_19_out, and_20_out);
  or or_3 (or_3_out, and_14_out, and_15_out);
  or or_4 (Z, and_12_out, and_22_out);
  and and_23 (and_23_out, D, or_2_out);
  or or_5 (Y, and_21_out, or_3_out);
  or or_6 (X, and_18_out, and_23_out);
endmodule
